# Fritzing sketch ASCIIKeyboard (saved by Fritzing 0.9.3b)
breadboards: 1

parts:
  S1 = Pushbutton [part_number=7 package="[THT]"]
  S2 = Pushbutton [part_number=6 package="[THT]"]
  S3 = Pushbutton [part_number=4 package="[THT]"]
  S4 = Pushbutton [part_number=5 package="[THT]"]
  S5 = Pushbutton [part_number=3 package="[THT]"]
  S6 = Pushbutton [part_number=2 package="[THT]"]
  S7 = Pushbutton [part_number=1 package="[THT]"]
  S8 = Pushbutton [part_number=0 package="[THT]"]
  S9 = Pushbutton [part_number=SET package="[THT]"]
  S10 = Pushbutton [part_number=CLEAR package="[THT]"]
  Raspberry_Pi_1 = Raspberry Pi 3 [part_number=RPI-3-V1.2]
  R1 = Resistor [tolerance=±0.5% resistance=10k package=THT]
  R2 = Resistor [tolerance=±0.5% resistance=10k package=THT]

nets:
  N1: S1.Pin_1, S1.Pin_2, S2.Pin_1, S2.Pin_2, S3.Pin_1, S3.Pin_2, S4.Pin_1, S4.Pin_2, S5.Pin_1, S5.Pin_2, S6.Pin_1, S6.Pin_2, S7.Pin_1, S7.Pin_2, S8.Pin_1, S8.Pin_2, S9.Pin_1, S9.Pin_2, S10.Pin_1, S10.Pin_2, Raspberry_Pi_1.GND, Raspberry_Pi_1.GPIO21, Raspberry_Pi_1.GPIO20
  N2: S1.Pin_3, S1.Pin_4, Raspberry_Pi_1.GPIO22
  N3: S2.Pin_3, S2.Pin_4, Raspberry_Pi_1.GPIO25
  N4: S3.Pin_3, S3.Pin_4, Raspberry_Pi_1.GPIO5
  N5: S4.Pin_3, S4.Pin_4, Raspberry_Pi_1.GPIO19
  N6: S5.Pin_3, S5.Pin_4, Raspberry_Pi_1.GPIO6
  N7: S6.Pin_3, S6.Pin_4, Raspberry_Pi_1.GPIO27
  N8: S7.Pin_3, S7.Pin_4, Raspberry_Pi_1.GPIO26
  N9: S8.Pin_3, S8.Pin_4, Raspberry_Pi_1.GPIO16
  N10: S9.Pin_3, S9.Pin_4, R2.Pin_1
  N11: S10.Pin_3, S10.Pin_4, R1.Pin_1
  N12: Raspberry_Pi_1.3v3, R1.Pin_0, R2.Pin_0

notes:
  Using Raspberry Pi 3 in place of PicoPro
